# Fritzing sketch DifferentialOpAmp (saved by Fritzing 0.9.3b)
breadboards: 1

parts:
  U1 = LM 358 Dual Op-Amp [package="DIP8 [THT]"]
  Part1 = Arduino Uno (Rev3) - ICSP
  R1 = Resistor [tolerance=±5% resistance=220 package=THT]
  R2 = Resistor [tolerance=±5% resistance=220 package=THT]
  R3 = Resistor [tolerance=±5% resistance=220 package=THT]
  R4 = Photocell (LDR) [package=THT]
  R5 = Resistor [tolerance=±5% resistance=220 package=THT]
  R6 = Resistor [tolerance=±5% resistance=220 package=THT]

nets:
  N1: U1.connector0, R6.Pin_1
  N2: U1.connector1, R1.Pin_0
  N3: U1.connector2, R5.Pin_1
  N4: U1.connector3, R2.Pin_0, R3.Pin_0
  N5: Part1.A0, R6.Pin_0
  N6: Part1.3V3, R4.pin_0
  N7: Part1.5V, R5.Pin_0
  N8: R1.Pin_1, R3.Pin_1
  N9: R2.Pin_1, R4.pin_1
