# Fritzing sketch differential (saved by Fritzing 0.9.3b)
breadboards: 1

parts:
  Part1 = Arduino Mega ADK (Rev3)
  U1 = LM 358 Dual Op-Amp [package="DIP8 [THT]"]
  R1 = Resistor [tolerance=±5% resistance=2k package=THT]
  R2 = Photocell (LDR) [package=THT]
  R3 = Resistor [tolerance=±5% resistance=7k package=THT]
  R4 = Resistor [tolerance=±5% resistance=1k package=THT]
  R5 = Resistor [tolerance=±5% resistance=1k package=THT]

nets:
  N1: Part1.A0, U1.connector0, R1.Pin_0
  N2: Part1.3V3, U1.connector7
  N3: Part1.5V, R2.pin_0, R3.Pin_1
  N4: Part1.GND, U1.connector3, R4.Pin_0, R5.Pin_1
  N5: U1.connector1, R1.Pin_1, R2.pin_1, R5.Pin_0
  N6: U1.connector2, R3.Pin_0, R4.Pin_1
